# Fritzing sketch iki_74hc595_ile_8_digit_7_segment_display (saved by Fritzing 0.9.2b)
breadboards: 1

parts:
  Q1 = NPN-Transistor [package="TO92 [THT]"]
  U1 = 74HC595 [package="DIP16 [THT]"]
  U2 = 74HC595 [package="DIP16 [THT]"]
  U4 = 7-SEGMENT-4DIGIT [package=7-segment-4digit]
  U5 = 7-SEGMENT-4DIGIT [package=7-segment-4digit]
  Eleman1 = Arduino UNO R3  # not connected
  Eleman2 = Thumb Joystick

nets:
  N1: Q1.E, U2.DS
  N2: Q1.B, U1.Q7'
  VCC: Q1.C, U1.MR, U1.VCC, U2.MR, U2.VCC, Eleman2.VCC
  N3: U1.Q1, U5.15
  N4: U1.Q3, U5.9
  N5: U1.Q4, U4.16
  N6: U1.Q5, U4.13
  GND: U1.GND, U2.GND
  N7: U1.SH_CP, U2.SH_CP
  N8: U1.ST_CP, U2.ST_CP
  N9: U1.OE, U2.OE

notes:
  Digit wires from digit0 to digit7 // Sayıların sırasıyla kabloları 0dan 7 ye.
  7segments respectively
  sırasıyla 7 segment ve DP
  Arduino Uno, 74HC595, BC546, 4digit7segmentDisplay, joystick used home made display module.
  Dr.Melik Çandar 2015 Turkey www.youtube.com/Melik Candar.
